// Digital circuit LED_Blinker.dig as structural Verilog
module LED_Blinker (
  input  _50MHz_Clock
);

  wire Comparator_eq, Toggle_FF_q;
  wire [24:0] Counter_to_25M_clock_cycles_out;

  Counter #(.Bits(25)) Counter_to_25M_clock_cycles (
    .en(1'b1), .C(_50MHz_Clock), .clr(Comparator_eq), .out(Counter_to_25M_clock_cycles_out));  // open: ovf
  Comparator #(.Bits(25)) Comparator (
    .a(Counter_to_25M_clock_cycles_out), .b(25'h61a8), .eq(Comparator_eq));  // open: gt, lt
  T_FF Toggle_FF (.T(Comparator_eq), .C(_50MHz_Clock), .Q(Toggle_FF_q));  // open: nQ
  LED LED (.in(Toggle_FF_q));

  // Notes on the sheet:
  //   _50MHz_Clock: Hz: 50000
  //   Cannot use above 50KHz because the simulator starts to lag.
endmodule
